# Fritzing sketch Arduino_Master_Clock (saved by Fritzing 0.9.4)
breadboards: 1

parts:
  Part1 = Arduino Nano (Rev3.0)
  Grove1 = Grove 4 Digit Display
  U1 = ENCODER-QUADRATURE [package=encoder-16mm-quad]
  S1 = Pushbutton [package="[THT]"]
  S2 = Pushbutton [package="[THT]"]
  TRS1 = Audio Jack (TRS) 3.5mm [package="PG203J [THT]"]
  TRS2 = Audio Jack (TRS) 3.5mm [package="PG203J [THT]"]
  U2 = MIDI_CONN_FEMALE [package=din_5_female]  # not connected
  R1 = Resistor [tolerance=±5% resistance=220 package=THT]
  R2 = Resistor [tolerance=±5% resistance=220 package=THT]

nets:
  N1: Part1.D1/TX, R1.Pin_0
  GND: Part1.GND, Grove1.GND, U1.B, S1.Pin_1, S1.Pin_2, S2.Pin_1, S2.Pin_2, TRS1.Sleeve, TRS2.Sleeve
  N2: Part1.D2, U1.C
  N3: Part1.D3, U1.A
  N4: Part1.D4, Grove1.CLK
  N5: Part1.D5, Grove1.DIO
  N6: Part1.D6, TRS1.Tip
  N7: Part1.D8, TRS2.Tip
  5V: Part1.5V, Grove1.VCC, R2.Pin_0
  N8: Part1.A5, S2.Pin_3, S2.Pin_4
  N9: Part1.A4, S1.Pin_3, S1.Pin_4
